// Logisim project ex_mem.circ as structural Verilog: 2 circuits, main circuit main
module main (
  input  in_1,
  input  WB,
  input  MEM_Read,
  input  MEM_Write,
  input  Reg_write,
  input  [4:0] Rd,
  input  [31:0] Alu_res,
  input  [31:0] BUSB_EX,
  output out_9,
  output out_10,
  output out_11,
  output out_12,
  output [4:0] out_13,
  output [31:0] out_14,
  output [31:0] out_15
);

  Register #(.width(1)) register_1 (.D(WB), .en(1'b1), .clk(in_1), .Q(out_9));  // open: clr
  Register #(.width(1)) register_2 (.D(MEM_Read), .en(1'b1), .clk(in_1), .Q(out_10));  // open: clr
  Register #(.width(1)) register_3 (.D(MEM_Write), .en(1'b1), .clk(in_1), .Q(out_11));  // open: clr
  Register #(.width(1)) register_4 (.D(Reg_write), .en(1'b1), .clk(in_1), .Q(out_12));  // open: clr
  Register #(.width(5)) register_5 (.D(Rd), .en(1'b1), .clk(in_1), .Q(out_13));  // open: clr
  Register #(.width(32)) register_6 (.D(Alu_res), .en(1'b1), .clk(in_1), .Q(out_14));  // open: clr
  Register #(.width(32)) register_7 (.D(BUSB_EX), .en(1'b1), .clk(in_1), .Q(out_15));  // open: clr

  // Other names for the same wires on the sheet: CLk = in_1
endmodule

module block (
);

  main main_1 ();  // open: in_1, WB, MEM_Read, MEM_Write, Reg_write, Rd, Alu_res, out_9, out_10, out_11, out_12, out_13, out_14, BUSB_EX, out_15
endmodule
